// Logisim project immediate_generator.circ as structural Verilog: 1 circuit, main circuit main
module main (
  input  [15:0] imm16,
  input  [1:0] ImmSel,
  output [31:0] ImmVal
);

  wire [31:0] bit_extender_1_out, bit_extender_2_out, shifter_1_out;

  assign bit_extender_1_out = {{16{imm16[15]}}, imm16};  // Bit_Extender bit_extender_1
  assign bit_extender_2_out = {{16{1'b0}}, imm16};  // Bit_Extender bit_extender_2
  Shifter #(.width(32)) shifter_1 (.in(bit_extender_1_out), .\dist (5'b00010), .out(shifter_1_out));
  Multiplexer #(.select(2), .width(32)) multiplexer_1 (
    .in0(bit_extender_1_out), .in1(bit_extender_2_out), .in2({imm16, {16{1'b0}}}), .in3(shifter_1_out),
    .out(ImmVal), .sel(ImmSel), .en(1'b1));
endmodule
